# Fritzing sketch blinkers-and-brakes-breadboard (saved by Fritzing 0.9.3b)
breadboards: 1

parts:
  LED1 = LED - 3mm [color="Red (633nm)" package="3 mm [THT]"]
  U2 = 555 Timer [package="DIP8 [THT]"]
  R3 = Resistor [tolerance=±5% resistance=470 package=THT]
  R1 = Resistor [tolerance=±5% resistance=470 package=THT]
  R2 = Resistor [tolerance=±5% resistance=470k package=THT]
  VCC1 = Battery block 9V
  C3 = Ceramic Capacitor [capacitance=100nF package="100 mil [THT, multilayer]"]
  LED5 = LED - 3mm [color="Red (633nm)" package="3 mm [THT]"]
  C2 = Electrolytic Capacitor [capacitance=1µF package="100 mil [THT, electrolytic]"]
  Part1 = Adafruit Metro with Headers [part_number="Adafruit #2488"]
  S1 = Toggle Switch [package=THT]
  Q1 = NPN-Transistor [package="TO92 [THT]"]
  Q2 = NPN-Transistor [package="TO92 [THT]"]
  R4 = Resistor [tolerance=±5% resistance=10k package=THT]
  R5 = Resistor [tolerance=±5% resistance=10k package=THT]
  R6 = Resistor [tolerance=±5% resistance=470 package=THT]
  LED6 = LED - 3mm [color="Red (633nm)" package="3 mm [THT]"]
  LED7 = LED - 3mm [color="Red (633nm)" package="3 mm [THT]"]
  Part2 = Adafruit Proto Shield R3 [part_number="Adafruit #2077"]  # not connected

nets:
  N1: LED1.cathode, Q1.E
  N2: LED1.anode, R3.Pin_1, LED5.anode
  N3: U2.Ground, VCC1.-, C3.1, C2.-, Part1.GND, Q1.C, Q2.C, LED7.cathode
  N4: U2.Trigger, U2.Threshold, R2.Pin_1, C2.+
  N5: U2.Output, R3.Pin_0
  N6: U2.Reset, U2.Vcc_Supply_Voltage, R1.Pin_0, S1.COM
  N7: U2.Control_Voltage, C3.0
  N8: U2.Discharge, R1.Pin_1, R2.Pin_0
  N9: VCC1.+, S1.L2
  N10: LED5.cathode, Q2.E
  N11: Part1.IO2, R6.Pin_0
  N12: Part1.IO1, R4.Pin_0
  N13: Part1.IO0, R5.Pin_0
  N14: Q1.B, R4.Pin_1
  N15: Q2.B, R5.Pin_1
  N16: R6.Pin_1, LED6.anode
  N17: LED6.cathode, LED7.anode

custom parts:
  Adafruit Metro with Headers: We sure love the ATmega328 here at Adafruit, and we use them a lot for our own projects. The processor has plenty of GPIO, Analog inputs, hardware UART SPI and I2C, timers and PWM galore - just enough for most simple projects. When we need to go small, we use a Pro Trinket 3V or 5V, but when size isn't as much of a concern, and an USB-serial converter is required, we reach for an Adafruit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
  Adafruit Proto Shield R3: This prototyping shield is the best out there (well, we think so, at least), and now is even better with Version R3 - updated for the most compatibility with just about all the Arduinos! It works with UNO, Mega, Leonardo, NG, Diecimila, Duemilanove, and compatible Arduinos. Yun's and Arduino Ethernets have a chunky Ethernet jack that gets in the way of stacking, you can use the stacking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
