# Fritzing sketch protoshield (saved by Fritzing 0.9.3b)

parts:
  Part3 = Adafruit Proto Shield R3 [part_number="Adafruit #2077"]
  IC3 = L293D [package=THT]
  VCC1 = Battery

nets:
  N1: Part3.P$5#1, IC3.+Vmotor
  N2: Part3.GND, Part3.1#132, Part3.P$5#133, Part3.1#183, Part3.1#193, Part3.P$5#194, Part3.1#205, Part3.P$5#206, Part3.N$177, IC3.0V, VCC1.-
  N3: Part3.+5V, Part3.P$5#124, Part3.1#166, Part3.P$5#167, Part3.N$16, Part3.P$5#197, IC3.Enable_1, IC3.Enable_2, IC3.+V
  N4: Part3.D0, Part3.N$144
  N5: Part3.D1, Part3.N$143
  N6: Part3.D2, Part3.N$175
  N7: Part3.D5, Part3.P$5#127, Part3.P$6#128, IC3.In_1
  N8: Part3.D6, Part3.P$5#164, Part3.P$6#165, IC3.In_2
  N9: Part3.D9, Part3.N$115, Part3.P$5#161, IC3.In_3
  N10: Part3.D10, Part3.1#180, Part3.P$5#181, IC3.In_4
  N11: Part3.1#129, Part3.P$5#130, Part3.N$49, IC3.Out_1_(_Controlled_by_Enable_1_)
  N12: Part3.1#172, Part3.P$5#173, Part3.N$165, IC3.Out_3_(_Controlled_by_Enable_2_)
  N13: Part3.N$15, Part3.P$5#200, Part3.N$159, IC3.Out_4_(_Controlled_by_Enable_2_)
  N14: Part3.1#202, Part3.P$5#203, Part3.N$21, IC3.Out_2_(_Controlled_by_Enable_1_)
  N15: Part3.N$136, VCC1.+
  N16: Part3.N$168, Part3.N$173

custom parts:
  Adafruit Proto Shield R3: This prototyping shield is the best out there (well, we think so, at least), and now is even better with Version R3 - updated for the most compatibility with just about all the Arduinos! It works with UNO, Mega, Leonardo, NG, Diecimila, Duemilanove, and compatible Arduinos. Yun's and Arduino Ethernets have a chunky Ethernet jack that gets in the way of stacking, you can use the stacking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
