# Fritzing sketch v-i (saved by Fritzing 0.9.3b)
breadboards: 1

parts:
  Part1 = Arduino Uno (Rev3)
  IC1 = L293D [package=THT]
  VCC1 = 4 x AAA Battery Mount
  M1 = DC Motor
  M2 = DC Motor

nets:
  N1: Part1.D9_PWM, IC1.In_3
  N2: Part1.D10_PWM/SS, IC1.In_4
  N3: Part1.D5_PWM, IC1.In_1
  N4: Part1.D6_PWM, IC1.In_2
  N5: Part1.5V, IC1.Enable_1, IC1.Enable_2, IC1.+V
  N6: Part1.GND, IC1.0V, VCC1.-
  N7: IC1.Out_1_(_Controlled_by_Enable_1_), M1.pin_2
  N8: IC1.Out_2_(_Controlled_by_Enable_1_), M1.pin_1
  N9: IC1.+Vmotor, VCC1.+
  N10: IC1.Out_3_(_Controlled_by_Enable_2_), M2.pin_2
  N11: IC1.Out_4_(_Controlled_by_Enable_2_), M2.pin_1
