# Fritzing sketch demo (saved by Fritzing 0.9.4)
breadboards: 1

parts:
  SERVO1 = Tower Pro SG90 servo [part_number=101246]  # not connected
  Part1 = Adafruit PCA9685 PWM/Servo Breakout [part_number=815]
  SERVO2 = Tower Pro SG90 servo [part_number=101246]  # not connected
  VCC1 = 4 x AAA Battery Mount
  Part2 = Arduino Nano (Rev3.0) (ICSP)
  R2 = TRIMPOT [package=3362u-2]
  R3 = TRIMPOT [package=3362u-2]

nets:
  N1: Part1.PWRIN, VCC1.+
  GND: Part1.GND, VCC1.-, Part2.GND, R2.CW, R3.CW
  VCC: Part1.VCC, Part2.5V, R2.CCW, R3.CCW
  N2: Part1.SDA, Part2.A4
  N3: Part1.SCL, Part2.A5
  N4: Part2.A1, R2.WIPER
  N5: Part2.A0, R3.WIPER

custom parts:
  Tower Pro SG90 servo: Original file by John De Cristofaro http://www.adafruit.com/products/1449 Adafruit Feedback Servo (Small) Edited by: e-radionica.com 28/9/2015
  Adafruit PCA9685 PWM/Servo Breakout: Using only two pins, control 16 free-running PWM outputs! I2C-controlled PWM driver with a built in clock. Unlike the TLC5940 family, you do not need to continuously send it signal tying up your microcontroller, its completely free running! 5V compliant, which means you can control it from a 3.3V microcontroller and still safely drive up to 6V outputs (this is good for when you want to control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
