# Fritzing sketch perfboard (saved by Fritzing 0.9.4)
perfboards: 1

parts:
  R1 = TRIMPOT [package=3362u-2]
  R2 = TRIMPOT [package=3362u-2]
  Part1 = Arduino Nano (Rev3.0)
  J3 = female pin header, 6 pins [form="♀ (female)"]
  BAT1 = BC9VPC [package=bc9vpc]
  VCC1 = 4 x AAA Battery Mount
  Part2 = Adafruit PCA9685 PWM/Servo Breakout [part_number=815]

nets:
  N1: R1.CCW, Part1.5V
  N2: R1.WIPER, Part1.A0
  N3: R1.CW, R2.CW, Part1.GND, BAT1.V-
  N4: R2.WIPER, Part1.A1
  N5: Part1.VIN, BAT1.V+
  N6: Part1.A5, J3.pin4, Part2.SCL
  N7: Part1.A4, J3.pin3, Part2.SDA
  N8: J3.pin1, Part2.5.0V
  N9: J3.pin2, Part2.VCC
  N10: J3.pin5, Part2.OE
  N11: J3.pin6, VCC1.-, Part2.GND
  N12: VCC1.+, Part2.PWRIN

custom parts:
  Adafruit PCA9685 PWM/Servo Breakout: Using only two pins, control 16 free-running PWM outputs! I2C-controlled PWM driver with a built in clock. Unlike the TLC5940 family, you do not need to continuously send it signal tying up your microcontroller, its completely free running! 5V compliant, which means you can control it from a 3.3V microcontroller and still safely drive up to 6V outputs (this is good for when you want to control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
