# Fritzing sketch blinkers-and-brakes (saved by Fritzing 0.9.3b)
perfboards: 1

parts:
  C2 = Electrolytic Capacitor [capacitance=1µF package="100 mil [THT, electrolytic]"]
  C3 = Ceramic Capacitor [capacitance=100nF package="100 mil [THT, multilayer]"]
  U1 = 555 Timer [package="DIP8 [THT]"]
  R3 = Resistor [tolerance=±5% resistance=470 package=THT]
  R4 = Resistor [tolerance=±5% resistance=470k package=THT]
  R5 = Resistor [tolerance=±5% resistance=470 package=THT]
  LED2 = LED - 3mm [color="Orange (620nm)" package="3 mm [THT]"]
  LED3 = LED - 3mm [color="Orange (620nm)" package="3 mm [THT]"]
  Q2 = NPN-Transistor [package="TO92 [THT]"]
  Q3 = NPN-Transistor [package="TO92 [THT]"]
  LED4 = LED - 3mm [color="Red (633nm)" package="3 mm [THT]"]
  LED5 = LED - 3mm [color="Red (633nm)" package="3 mm [THT]"]
  R6 = Resistor [tolerance=±5% resistance=10k package=THT]
  R7 = Resistor [tolerance=±5% resistance=10k package=THT]
  R8 = Resistor [tolerance=±5% resistance=470 package=THT]
  J1 = female pin header, 5 pins [form="♀ (female)"]

nets:
  N1: C2.+, J1.pin5
  N2: C3.0, U1.Control_Voltage
  N3: C3.1, LED5.cathode
  N4: U1.Ground, Q2.C
  N5: U1.Trigger, U1.Threshold
  N6: U1.Output, R5.Pin_1
  N7: U1.Discharge, R4.Pin_0
  N8: R3.Pin_0, J1.pin4
  N9: R5.Pin_0, LED2.anode, LED3.anode
  N10: LED2.cathode, Q3.E
  N11: LED3.cathode, Q2.E
  N12: Q2.B, R6.Pin_1
  N13: Q3.B, R7.Pin_1
  N14: LED4.cathode, LED5.anode
  N15: R6.Pin_0, J1.pin1
  N16: R7.Pin_0, J1.pin2
  N17: R8.Pin_1, J1.pin3
