# Fritzing sketch breadboard (saved by Fritzing 0.9.3b)
breadboards: 1

parts:
  Part1 = Arduino Uno (Rev3)
  IC1 = L293D [package=THT]
  VCC1 = 4 x AAA Battery Mount
  M1 = DC Motor
  M2 = DC Motor
  Part2 = Adafruit Proto Shield R3 [part_number="Adafruit #2077"]
  IC2 = L293D [package=THT]

nets:
  N1: Part1.D9_PWM, IC1.In_3
  N2: Part1.D10_PWM/SS, IC1.In_4
  N3: Part1.D5_PWM, IC1.In_1
  N4: Part1.D6_PWM, IC1.In_2
  N5: Part1.5V, IC1.Enable_1, IC1.Enable_2, IC1.+V
  N6: Part1.GND, IC1.0V, VCC1.-
  N7: IC1.Out_1_(_Controlled_by_Enable_1_), M1.pin_2
  N8: IC1.Out_2_(_Controlled_by_Enable_1_), M1.pin_1
  N9: IC1.+Vmotor, VCC1.+
  N10: IC1.Out_3_(_Controlled_by_Enable_2_), M2.pin_2
  N11: IC1.Out_4_(_Controlled_by_Enable_2_), M2.pin_1
  N12: Part2.P$5#1, Part2.P$6#2, IC2.+Vmotor
  N13: Part2.GND, Part2.1#132, Part2.P$5#133, Part2.1#183, Part2.1#193, Part2.1#205, Part2.P$5#206, IC2.0V
  N14: Part2.D5, Part2.1#126, Part2.P$5#127, IC2.In_1
  N15: Part2.D6, Part2.1#163, Part2.P$5#164, IC2.In_2
  N16: Part2.D9, Part2.N$115, Part2.P$5#161, IC2.In_3
  N17: Part2.D10, Part2.1#180, Part2.P$5#181, IC2.In_4
  N18: Part2.P$5#124, Part2.1#166, Part2.P$5#167, Part2.+5V, Part2.N$16, Part2.P$5#197, IC2.Enable_1, IC2.Enable_2, IC2.+V
  N19: Part2.P$5#130, Part2.P$6#131, IC2.Out_1_(_Controlled_by_Enable_1_)
  N20: Part2.1#172, Part2.P$6#174, IC2.Out_3_(_Controlled_by_Enable_2_)
  N21: Part2.N$15, Part2.P$6#201, IC2.Out_4_(_Controlled_by_Enable_2_)
  N22: Part2.P$5#203, Part2.P$6#204, IC2.Out_2_(_Controlled_by_Enable_1_)

custom parts:
  Adafruit Proto Shield R3: This prototyping shield is the best out there (well, we think so, at least), and now is even better with Version R3 - updated for the most compatibility with just about all the Arduinos! It works with UNO, Mega, Leonardo, NG, Diecimila, Duemilanove, and compatible Arduinos. Yun's and Arduino Ethernets have a chunky Ethernet jack that gets in the way of stacking, you can use the stacking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
