# Fritzing sketch protoshield-extras-corrected (saved by Fritzing 0.9.3b)

parts:
  S1 = Pushbutton [package="[THT]"]
  R1 = Resistor [tolerance=±5% resistance=10k package=THT]
  Part1 = Adafruit Proto Shield R3 [part_number="Adafruit #2077"]
  LED1 = LED - 5mm [color="Red (633nm)" package="5 mm [THT]"]
  LED2 = LED - 5mm [color="Green (555nm)" package="5 mm [THT]"]
  R2 = Resistor [tolerance=±5% resistance=220 package=THT]
  R3 = Resistor [tolerance=±5% resistance=220 package=THT]
  hc-sr1 = hc-sr04

nets:
  N1: S1.Pin_1, S1.Pin_2, R1.Pin_0, Part1.D4, Part1.N$9, Part1.N$39, Part1.N$53
  N2: S1.Pin_3, S1.Pin_4, Part1.1, Part1.P$5, Part1.P$6, Part1.+5V, Part1.N$42, Part1.N$48, Part1.N$121
  N3: Part1.GND, Part1.N$29, Part1.N$124, Part1.N$172, Part1.N$193, R2.Pin_1, R3.Pin_1
  N4: Part1.D7, Part1.N$120
  N5: Part1.D13, Part1.N$157, LED1.anode
  N6: Part1.D12, Part1.N$6, LED2.anode
  N7: Part1.D8, Part1.N$122
  N8: Part1.N$3, LED1.cathode
  N9: Part1.N$7, LED2.cathode
  N10: Part1.N$91, R3.Pin_0
  N11: Part1.N$100, R2.Pin_0
  N12: Part1.N$114, hc-sr1.VCC
  N13: Part1.N$118, hc-sr1.Trig
  N14: Part1.N$119, hc-sr1.Echo
  N15: Part1.N$123, hc-sr1.GND

custom parts:
  Adafruit Proto Shield R3: This prototyping shield is the best out there (well, we think so, at least), and now is even better with Version R3 - updated for the most compatibility with just about all the Arduinos! It works with UNO, Mega, Leonardo, NG, Diecimila, Duemilanove, and compatible Arduinos. Yun's and Arduino Ethernets have a chunky Ethernet jack that gets in the way of stacking, you can use the stacking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
